// Logisim project 计原课设P1.circ as structural Verilog: 13 circuits, main circuit main
module main (
  input  Reset
);

  wire CLK, ExtOp, isBeq, isImm, isJ, isJr, isMem, MemWr, RegDst, RegWr, Zero;
  wire [1:0] ALUSel;
  wire [4:0] multiplexer_1_out, rd, rs, rt;
  wire [15:0] imm;
  wire [25:0] Addr;
  wire [31:0] alu_1_c, dm_1_loaddata, extender_1__32imm, ifu_1_instr, multiplexer_2_out, multiplexer_3_out,
       RAddr, regfile_1_rd2;

  Clock u_CLK (.out(CLK));
  Multiplexer #(.width(5), .enable("false")) multiplexer_1 (.in0(rd), .in1(rt), .out(multiplexer_1_out), .sel(RegDst));
  // Probe on ifu_1_instr
  IFU ifu_1 (
    .imm(imm), .tara(Addr), .IfJ(isJ), .IfBeq(isBeq), .Instr(ifu_1_instr), .CLK(CLK), .Reset(Reset),
    .Zero(Zero), .IfJr(isJr), .RAddr(RAddr));
  RegFile regfile_1 (
    .Write_Enable(RegWr), .busW(multiplexer_3_out), .RW(multiplexer_1_out), .RB(rt), .RD1(RAddr),
    .RD2(regfile_1_rd2), .RA(rs), .CLK(CLK));
  Extender extender_1 (.imm(imm), ._32imm(extender_1__32imm), .ExtOp(ExtOp));
  Control control_1 (
    .Instru(ifu_1_instr), .RegDst(RegDst), .target_address(Addr), .rs(rs), .rt(rt), .ALUSel(ALUSel),
    .imm(imm), .rd(rd), .isImm(isImm), .RegWr(RegWr), .ExtOp(ExtOp), .MemWr(MemWr), .isMem(isMem),
    .isBeq(isBeq), .isJ(isJ), .isJr(isJr));  // open: shamt
  Multiplexer #(.width(32), .enable("false")) multiplexer_2 (
    .in0(regfile_1_rd2), .in1(extender_1__32imm), .out(multiplexer_2_out), .sel(isImm));
  ALU alu_1 (.A(RAddr), .B(multiplexer_2_out), .C(alu_1_c), .F(ALUSel), .Zero(Zero));
  Multiplexer #(.width(32), .enable("false")) multiplexer_3 (
    .in0(alu_1_c), .in1(dm_1_loaddata), .out(multiplexer_3_out), .sel(isMem));
  DM dm_1 (.Address(alu_1_c[4:0]), .WriteData(regfile_1_rd2), .LoadData(dm_1_loaddata), .WriteEN(MemWr), .clk(CLK));
endmodule

module ALU (
  input  [31:0] A,
  input  [1:0] F,
  input  [31:0] B,
  output [31:0] C,
  output Zero
);

  wire [31:0] adder_1_s, or_1_out, shifter_1_out, subtracter_1_s;

  Comparator #(.width(32), .mode("unsigned")) comparator_1 (.a(A), .b(B), .eq(Zero));  // open: gt, lt
  assign or_1_out = A | B;  // OR_Gate or_1, 32 bits wide
  Shifter #(.width(32)) shifter_1 (.in(B), .\dist (5'b10000), .out(shifter_1_out));
  Adder adder_1 (.Cin(1'b0), .S(adder_1_s), .A(A), .B(B));  // open: Cout
  Subtracter subtracter_1 (.S(subtracter_1_s), .A(A), .B(B));
  Multiplexer #(.select(2), .width(32), .enable("false")) multiplexer_1 (
    .in0(adder_1_s), .in1(subtracter_1_s), .in2(or_1_out), .in3(shifter_1_out), .out(C), .sel(F));
endmodule

module IFU (
  input  [15:0] imm,
  input  [25:0] tara,
  input  IfBeq,
  input  IfJ,
  input  Zero,
  input  IfJr,
  input  [31:0] RAddr,
  input  CLK,
  input  Reset,
  output [31:0] Instr
);

  wire and_1_out;
  wire [1:0] priority_encoder_1_out;
  wire [29:0] adder_2_out, adder_3_out, bit_extender_1_out, bit_extender_3_out, imm_address,
       multiplexer_1_out, PC_q, \PC高位 , target_address;

  assign bit_extender_1_out = {{4{1'b0}}, tara};  // Bit_Extender bit_extender_1
  assign imm_address = {{14{imm[15]}}, imm};  // Bit_Extender bit_extender_2
  Adder_part #(.width(30)) adder_1 (.a(\PC高位 ), .b(bit_extender_1_out), .out(target_address));  // open: cin, cout
  and and_1 (and_1_out, IfBeq, Zero);
  Multiplexer #(.select(2), .width(30), .enable("false")) multiplexer_1 (
    .in0(adder_3_out), .in1(target_address), .in2(adder_2_out), .in3(RAddr[31:2]), .out(multiplexer_1_out),
    .sel(priority_encoder_1_out));
  Priority_Encoder #(.select(2)) priority_encoder_1 (
    .in0(1'b1), .in1(IfJ), .in2(and_1_out), .in3(IfJr), .out(priority_encoder_1_out));  // open: gs, en_out, en_in
  Adder_part #(.width(30)) adder_2 (.a(imm_address), .b(adder_3_out), .out(adder_2_out));  // open: cin, cout
  Register #(.width(30)) PC (.D(multiplexer_1_out), .en(1'b1), .Q(PC_q), .clk(CLK), .clr(Reset));
  Adder_part #(.width(30)) adder_3 (.a(30'h1), .b(PC_q), .out(adder_3_out));  // open: cin, cout
  // Probe on PC_q[4:0]
  assign bit_extender_3_out = {{26{1'b0}}, PC_q[29:26]};  // Bit_Extender bit_extender_3
  Shifter #(.width(30)) shifter_1 (.in(bit_extender_3_out), .\dist (5'b11010), .out(\PC高位 ));
  ROM #(.addrWidth(5), .dataWidth(32)) rom_1 (.addr(PC_q[4:0]), .data(Instr), .sel(1'b1));

  // Notes on the sheet:
  //   contents of rom_1 (hex, n*v repeats v):
  //   8d310000 2328021 2318023 3610000f 3c12000f 2110021 2125021 22a5823 12110006 12600001 8000c00
  //   ad300000 2128023 9021 8000c00 2108021 2118821 2329021 36130001 ad300000 12a4823 112affea
endmodule

module Extender (
  input  [15:0] imm,
  input  ExtOp,
  output [31:0] _32imm
);

  wire [31:0] bit_extender_1_out, bit_extender_2_out;

  assign bit_extender_1_out = {{16{1'b0}}, imm};  // Bit_Extender bit_extender_1
  assign bit_extender_2_out = {{16{imm[15]}}, imm};  // Bit_Extender bit_extender_2
  Multiplexer #(.width(32), .enable("false")) multiplexer_1 (
    .in0(bit_extender_1_out), .in1(bit_extender_2_out), .out(_32imm), .sel(ExtOp));
endmodule

module DM (
  input  [4:0] Address,
  input  [31:0] WriteData,
  input  WriteEN,
  input  clk,
  output [31:0] LoadData
);

  RAM #(.addrWidth(5), .dataWidth(32), .bus("separate")) ram_1 (
    .addr(Address), .din(WriteData), .data(LoadData), .str(WriteEN), .clk(clk));  // open: sel, ld, clr
endmodule

module FA (
  input  A,
  input  B,
  input  C,
  output S,
  output G,
  output P
);

  wire xor_1_out;

  xor xor_1 (xor_1_out, A, B);
  and and_1 (G, A, B);
  or or_1 (P, A, B);
  xor xor_2 (S, xor_1_out, C);
endmodule

module CLA (
  input  C0,
  input  G3,
  input  P3,
  input  G2,
  input  P2,
  input  G1,
  input  P1,
  input  G0,
  input  P0,
  output G,
  output P,
  output C4,
  output C3,
  output C2,
  output C1
);

  wire and_1_out, and_2_out, and_3_out, and_5_out, and_6_out, and_7_out, and_8_out, and_9_out, and_10_out,
       and_11_out, and_12_out, and_13_out, and_14_out;

  or or_1 (G, G3, and_1_out, and_2_out, and_3_out);
  and and_1 (and_1_out, P3, G2);
  and and_2 (and_2_out, P3, P2, G1);
  and and_3 (and_3_out, P3, P2, P1, G0);
  and and_4 (P, P3, P2, P1, P0);
  and and_5 (and_5_out, P3, G2);
  or or_2 (C4, G3, and_5_out, and_7_out, and_6_out, and_8_out);
  and and_6 (and_6_out, P3, P2, P1, G0);
  and and_7 (and_7_out, P3, P2, G1);
  and and_8 (and_8_out, P3, P2, P1, P0, C0);
  and and_9 (and_9_out, P2, G1);
  or or_3 (C3, G2, and_9_out, and_10_out, and_11_out);
  and and_10 (and_10_out, P2, P1, G0);
  and and_11 (and_11_out, P2, P1, P0, C0);
  or or_4 (C2, G1, and_12_out, and_13_out);
  and and_12 (and_12_out, P1, G0);
  and and_13 (and_13_out, P1, P0, C0);
  or or_5 (C1, G0, and_14_out);
  and and_14 (and_14_out, P0, C0);
endmodule

module _4BitAdder (
  input  [3:0] A,
  input  [3:0] B,
  input  C0,
  output [3:0] S,
  output C4,
  output G,
  output P
);

  wire cla_1_c1, cla_1_c2, cla_1_c3, fa_1_g, fa_1_p, fa_2_g, fa_2_p, fa_3_g, fa_3_p, fa_4_g, fa_4_p;

  FA fa_1 (.B(B[3]), .C(cla_1_c3), .S(S[3]), .G(fa_1_g), .P(fa_1_p), .A(A[3]));
  FA fa_2 (.B(B[2]), .C(cla_1_c2), .S(S[2]), .G(fa_2_g), .P(fa_2_p), .A(A[2]));
  FA fa_3 (.B(B[1]), .C(cla_1_c1), .S(S[1]), .G(fa_3_g), .P(fa_3_p), .A(A[1]));
  CLA cla_1 (
    .C0(C0), .C4(C4), .C3(cla_1_c3), .C2(cla_1_c2), .C1(cla_1_c1), .G3(fa_1_g), .P3(fa_1_p), .G2(fa_2_g),
    .P2(fa_2_p), .G1(fa_3_g), .P1(fa_3_p), .G0(fa_4_g), .P0(fa_4_p), .G(G), .P(P));
  FA fa_4 (.B(B[0]), .C(C0), .S(S[0]), .G(fa_4_g), .P(fa_4_p), .A(A[0]));
endmodule

module Adder (
  input  [31:0] A,
  input  [31:0] B,
  input  Cin,
  output [31:0] S,
  output Cout
);

  wire cla_1_c1, cla_1_c2, cla_1_c3, cla_1_g, cla_1_p, cla_2_c1, cla_3_c1, cla_3_c2, cla_3_c3, cla_3_g,
       cla_3_p, n4bitadder_1_g, n4bitadder_1_p, n4bitadder_2_g, n4bitadder_2_p, n4bitadder_3_g,
       n4bitadder_3_p, n4bitadder_4_g, n4bitadder_4_p, n4bitadder_5_g, n4bitadder_5_p, n4bitadder_6_g,
       n4bitadder_6_p, n4bitadder_7_g, n4bitadder_7_p, n4bitadder_8_g, n4bitadder_8_p;

  _4BitAdder u_4bitadder_1 (
    .C0(cla_1_c3), .S(S[31:28]), .A(A[31:28]), .B(B[31:28]), .G(n4bitadder_1_g), .P(n4bitadder_1_p));  // open: C4
  _4BitAdder u_4bitadder_2 (
    .C0(cla_1_c2), .S(S[27:24]), .A(A[27:24]), .B(B[27:24]), .G(n4bitadder_2_g), .P(n4bitadder_2_p));  // open: C4
  _4BitAdder u_4bitadder_3 (
    .C0(cla_1_c1), .S(S[23:20]), .A(A[23:20]), .B(B[23:20]), .G(n4bitadder_3_g), .P(n4bitadder_3_p));  // open: C4
  _4BitAdder u_4bitadder_4 (
    .C0(cla_2_c1), .S(S[19:16]), .A(A[19:16]), .B(B[19:16]), .G(n4bitadder_4_g), .P(n4bitadder_4_p));  // open: C4
  CLA cla_1 (
    .C0(cla_2_c1), .C3(cla_1_c3), .C2(cla_1_c2), .C1(cla_1_c1), .G3(n4bitadder_1_g), .P3(n4bitadder_1_p),
    .G2(n4bitadder_2_g), .P2(n4bitadder_2_p), .G1(n4bitadder_3_g), .P1(n4bitadder_3_p), .G0(n4bitadder_4_g),
    .P0(n4bitadder_4_p), .G(cla_1_g), .P(cla_1_p));  // open: C4
  _4BitAdder u_4bitadder_5 (
    .C0(cla_3_c3), .S(S[15:12]), .A(A[15:12]), .B(B[15:12]), .G(n4bitadder_5_g), .P(n4bitadder_5_p));  // open: C4
  _4BitAdder u_4bitadder_6 (
    .C0(cla_3_c2), .S(S[11:8]), .A(A[11:8]), .B(B[11:8]), .G(n4bitadder_6_g), .P(n4bitadder_6_p));  // open: C4
  CLA cla_2 (
    .C0(Cin), .C2(Cout), .C1(cla_2_c1), .G1(cla_1_g), .P1(cla_1_p), .G0(cla_3_g), .P0(cla_3_p));  // open: C4, C3, G3, P3, G2, P2, G, P
  _4BitAdder u_4bitadder_7 (
    .C0(cla_3_c1), .S(S[7:4]), .A(A[7:4]), .B(B[7:4]), .G(n4bitadder_7_g), .P(n4bitadder_7_p));  // open: C4
  _4BitAdder u_4bitadder_8 (
    .C0(Cin), .S(S[3:0]), .A(A[3:0]), .B(B[3:0]), .G(n4bitadder_8_g), .P(n4bitadder_8_p));  // open: C4
  CLA cla_3 (
    .C0(Cin), .C3(cla_3_c3), .C2(cla_3_c2), .C1(cla_3_c1), .G3(n4bitadder_5_g), .P3(n4bitadder_5_p),
    .G2(n4bitadder_6_g), .P2(n4bitadder_6_p), .G1(n4bitadder_7_g), .P1(n4bitadder_7_p), .G0(n4bitadder_8_g),
    .P0(n4bitadder_8_p), .G(cla_3_g), .P(cla_3_p));  // open: C4
endmodule

module Subtracter (
  input  [31:0] B,
  input  [31:0] A,
  output [31:0] S
);

  wire [31:0] adder_1_s, not_1_out;

  assign not_1_out = ~B;  // NOT_Gate not_1, 32 bits wide
  Adder adder_1 (.Cin(1'b0), .S(adder_1_s), .A(not_1_out), .B(32'h1));  // open: Cout
  Adder adder_2 (.Cin(1'b0), .S(S), .A(A), .B(adder_1_s));  // open: Cout
endmodule

module Control (
  input  [31:0] Instru,
  output RegDst,
  output [25:0] target_address,
  output [4:0] rs,
  output [4:0] rt,
  output [1:0] ALUSel,
  output [15:0] imm,
  output [4:0] rd,
  output [4:0] shamt,
  output isImm,
  output RegWr,
  output ExtOp,
  output MemWr,
  output isMem,
  output isBeq,
  output isJ,
  output isJr
);

  wire addu, lui, not_1_out, not_2_out, not_3_out, not_4_out, not_5_out, not_6_out, not_7_out, not_8_out,
       not_9_out, not_10_out, not_11_out, not_12_out, not_13_out, not_14_out, not_15_out, not_16_out,
       not_17_out, not_18_out, not_19_out, not_20_out, not_21_out, not_22_out, not_23_out, not_24_out,
       not_25_out, not_26_out, not_27_out, not_28_out, not_29_out, not_30_out, not_31_out, not_32_out,
       not_33_out, not_34_out, not_35_out, not_36_out, not_37_out, not_38_out, not_39_out, not_40_out,
       not_41_out, not_42_out, not_43_out, not_44_out, not_45_out, not_46_out, not_47_out, not_48_out,
       not_49_out, not_50_out, not_51_out, or_1_out, ori, subu;

  not not_1 (not_1_out, Instru[31]);
  not not_2 (not_2_out, Instru[30]);
  not not_3 (not_3_out, Instru[29]);
  not not_4 (not_4_out, Instru[28]);
  not not_5 (not_5_out, Instru[27]);
  not not_6 (not_6_out, Instru[26]);
  not not_7 (not_7_out, Instru[4]);
  not not_8 (not_8_out, Instru[3]);
  not not_9 (not_9_out, Instru[2]);
  not not_10 (not_10_out, Instru[1]);
  not not_11 (not_11_out, Instru[31]);
  not not_12 (not_12_out, Instru[30]);
  not not_13 (not_13_out, Instru[29]);
  not not_14 (not_14_out, Instru[28]);
  not not_15 (not_15_out, Instru[27]);
  not not_16 (not_16_out, Instru[26]);
  not not_17 (not_17_out, Instru[4]);
  not not_18 (not_18_out, Instru[3]);
  not not_19 (not_19_out, Instru[2]);
  not not_20 (not_20_out, Instru[31]);
  not not_21 (not_21_out, Instru[30]);
  not not_22 (not_22_out, Instru[27]);
  not not_23 (not_23_out, Instru[31]);
  not not_24 (not_24_out, Instru[30]);
  not not_25 (not_25_out, Instru[30]);
  not not_26 (not_26_out, Instru[28]);
  not not_27 (not_27_out, Instru[30]);
  not not_28 (not_28_out, Instru[29]);
  not not_29 (not_29_out, Instru[28]);
  not not_30 (not_30_out, Instru[31]);
  not not_31 (not_31_out, Instru[30]);
  not not_32 (not_32_out, Instru[29]);
  not not_33 (not_33_out, Instru[27]);
  not not_34 (not_34_out, Instru[26]);
  not not_35 (not_35_out, Instru[31]);
  not not_36 (not_36_out, Instru[30]);
  not not_37 (not_37_out, Instru[29]);
  not not_38 (not_38_out, Instru[28]);
  not not_39 (not_39_out, Instru[26]);
  not not_40 (not_40_out, Instru[31]);
  not not_41 (not_41_out, Instru[30]);
  not not_42 (not_42_out, Instru[29]);
  not not_43 (not_43_out, Instru[28]);
  not not_44 (not_44_out, Instru[27]);
  not not_45 (not_45_out, Instru[26]);
  not not_46 (not_46_out, Instru[5]);
  not not_47 (not_47_out, Instru[4]);
  not not_48 (not_48_out, Instru[2]);
  not not_49 (not_49_out, Instru[2]);
  not not_50 (not_50_out, Instru[1]);
  not not_51 (not_51_out, Instru[0]);
  // Probe on ori
  and and_1 (ori, not_20_out, not_21_out, Instru[29], Instru[28], not_22_out, Instru[26]);
  // Probe on lui
  and and_2 (lui, not_23_out, not_24_out, Instru[29], Instru[28], Instru[27], Instru[26]);
  // Probe on MemWr
  and and_3 (MemWr, Instru[31], not_25_out, Instru[29], not_26_out, Instru[27], Instru[26]);
  // Probe on isMem
  and and_4 (isMem, Instru[31], not_27_out, not_28_out, not_29_out, Instru[27], Instru[26]);
  // Probe on isBeq
  and and_5 (isBeq, not_30_out, not_31_out, not_32_out, Instru[28], not_33_out, not_34_out);
  // Probe on isJ
  and and_6 (isJ, not_35_out, not_36_out, not_37_out, not_38_out, Instru[27], not_39_out);
  // Probe on addu
  and and_7 (addu, not_1_out, not_2_out, not_3_out, not_4_out, not_5_out, not_6_out, Instru[5], not_7_out, not_8_out, not_9_out, not_10_out, Instru[0]);
  // Probe on subu
  and and_8 (subu, not_11_out, not_12_out, not_13_out, not_14_out, not_15_out, not_16_out, Instru[5], not_17_out, not_18_out, not_19_out, Instru[1], Instru[0]);
  // Probe on isJr
  and and_9 (isJr, not_40_out, not_41_out, not_42_out, not_43_out, not_44_out, not_45_out, not_46_out, not_47_out, Instru[3], not_48_out, not_49_out, not_50_out, not_51_out);
  or or_1 (or_1_out, MemWr, isMem, addu);
  or or_2 (RegDst, MemWr, isMem, isBeq, ori, lui);
  Priority_Encoder #(.select(2)) priority_encoder_1 (
    .in0(or_1_out), .in1(subu), .in2(ori), .in3(lui), .out(ALUSel));  // open: gs, en_out, en_in
  or or_3 (isImm, ori, lui, isMem, MemWr);
  or or_4 (RegWr, ori, lui, addu, subu, isMem);
  or or_5 (ExtOp, MemWr, isMem);

  assign imm = Instru[15:0];
  assign rd = Instru[15:11];
  assign rs = Instru[25:21];
  assign rt = Instru[20:16];
  assign shamt = Instru[10:6];
  assign target_address = Instru[25:0];

  // Other names for the same wires on the sheet: beq = isBeq; j = isJ; jr = isJr; lw = isMem; sw = MemWr
endmodule

module RegFile (
  input  Write_Enable,
  input  CLK,
  input  [4:0] RA,
  input  [31:0] busW,
  input  [4:0] RW,
  input  [4:0] RB,
  output [31:0] RD1,
  output [31:0] RD2
);

  wire [31:0] _0R, _0W, _1R, _1W, _2R, _2W, _3R, _3W, _4R, _4W, _5R, _5W, _6R, _6W, _7R, _7W, _8R, _8W, _9R,
       _9W, _10R, _10W, _11R, _11W, _12R, _12W, _13R, _13W, _14R, _14W, _15R, _15W, _16R, _16W, _17R, _17W,
       _18R, _18W, _19R, _19W, _20R, _20W, _21R, _21W, _22R, _22W, _23R, _23W, _24R, _24W, _25R, _25W, _26R,
       _26W, _27R, _27W, _28R, _28W, _29R, _29W, _30R, _30W, _31R, _31W;

  Demultiplexer #(.select(5), .width(32), .tristate("true"), .enable("false")) demultiplexer_1 (
    .out0(_0W), .out1(_1W), .out2(_2W), .out3(_3W), .out4(_4W), .out5(_5W), .out6(_6W), .out7(_7W),
    .out8(_8W), .out9(_9W), .out10(_10W), .out11(_11W), .out12(_12W), .out13(_13W), .out14(_14W),
    .out15(_15W), .out16(_16W), .out17(_17W), .out18(_18W), .out19(_19W), .out20(_20W), .out21(_21W),
    .out22(_22W), .out23(_23W), .out24(_24W), .out25(_25W), .out26(_26W), .out27(_27W), .out28(_28W),
    .out29(_29W), .out30(_30W), .out31(_31W), .in(busW), .sel(RW));
  Register #(.width(32)) _0 (.D(_0W), .en(Write_Enable), .Q(_0R), .clk(CLK), .clr(1'b1));
  Register #(.width(32)) _8 (.D(_8W), .en(Write_Enable), .Q(_8R), .clk(CLK));  // open: clr
  Register #(.width(32)) _16 (.D(_16W), .en(Write_Enable), .Q(_16R), .clk(CLK));  // open: clr
  Register #(.width(32)) _24 (.D(_24W), .en(Write_Enable), .Q(_24R), .clk(CLK));  // open: clr
  Register #(.width(32)) _1 (.D(_1W), .en(Write_Enable), .Q(_1R), .clk(CLK));  // open: clr
  Register #(.width(32)) _9 (.D(_9W), .en(Write_Enable), .Q(_9R), .clk(CLK));  // open: clr
  Register #(.width(32)) _17 (.D(_17W), .en(Write_Enable), .Q(_17R), .clk(CLK));  // open: clr
  Register #(.width(32)) _25 (.D(_25W), .en(Write_Enable), .Q(_25R), .clk(CLK));  // open: clr
  Register #(.width(32)) _3 (.D(_3W), .en(Write_Enable), .Q(_3R), .clk(CLK));  // open: clr
  Register #(.width(32)) _2 (.D(_2W), .en(Write_Enable), .Q(_2R), .clk(CLK));  // open: clr
  Register #(.width(32)) _11 (.D(_11W), .en(Write_Enable), .Q(_11R), .clk(CLK));  // open: clr
  Register #(.width(32)) _10 (.D(_10W), .en(Write_Enable), .Q(_10R), .clk(CLK));  // open: clr
  Register #(.width(32)) _19 (.D(_19W), .en(Write_Enable), .Q(_19R), .clk(CLK));  // open: clr
  Register #(.width(32)) _18 (.D(_18W), .en(Write_Enable), .Q(_18R), .clk(CLK));  // open: clr
  Register #(.width(32)) _26 (.D(_26W), .en(Write_Enable), .Q(_26R), .clk(CLK));  // open: clr
  Register #(.width(32)) _27 (.D(_27W), .en(Write_Enable), .Q(_27R), .clk(CLK));  // open: clr
  Register #(.width(32)) _4 (.D(_4W), .en(Write_Enable), .Q(_4R), .clk(CLK));  // open: clr
  Register #(.width(32)) _12 (.D(_12W), .en(Write_Enable), .Q(_12R), .clk(CLK));  // open: clr
  Register #(.width(32)) _20 (.D(_20W), .en(Write_Enable), .Q(_20R), .clk(CLK));  // open: clr
  Register #(.width(32)) _28 (.D(_28W), .en(Write_Enable), .Q(_28R), .clk(CLK));  // open: clr
  Register #(.width(32)) _5 (.D(_5W), .en(Write_Enable), .Q(_5R), .clk(CLK));  // open: clr
  Register #(.width(32)) _13 (.D(_13W), .en(Write_Enable), .Q(_13R), .clk(CLK));  // open: clr
  Register #(.width(32)) _21 (.D(_21W), .en(Write_Enable), .Q(_21R), .clk(CLK));  // open: clr
  Register #(.width(32)) _29 (.D(_29W), .en(Write_Enable), .Q(_29R), .clk(CLK));  // open: clr
  Register #(.width(32)) _6 (.D(_6W), .en(Write_Enable), .Q(_6R), .clk(CLK));  // open: clr
  Register #(.width(32)) _14 (.D(_14W), .en(Write_Enable), .Q(_14R), .clk(CLK));  // open: clr
  Register #(.width(32)) _22 (.D(_22W), .en(Write_Enable), .Q(_22R), .clk(CLK));  // open: clr
  Register #(.width(32)) _30 (.D(_30W), .en(Write_Enable), .Q(_30R), .clk(CLK));  // open: clr
  Register #(.width(32)) _7 (.D(_7W), .en(Write_Enable), .Q(_7R), .clk(CLK));  // open: clr
  Register #(.width(32)) _15 (.D(_15W), .en(Write_Enable), .Q(_15R), .clk(CLK));  // open: clr
  Register #(.width(32)) _23 (.D(_23W), .en(Write_Enable), .Q(_23R), .clk(CLK));  // open: clr
  Register #(.width(32)) _31 (.D(_31W), .en(Write_Enable), .Q(_31R), .clk(CLK));  // open: clr
  Multiplexer #(.select(5), .width(32), .enable("false")) multiplexer_1 (
    .in0(_0R), .in1(_1R), .in2(_2R), .in3(_3R), .in4(_4R), .in5(_5R), .in6(_6R), .in7(_7R), .in8(_8R),
    .in9(_9R), .in10(_10R), .in11(_11R), .in12(_12R), .in13(_13R), .in14(_14R), .in15(_15R), .in16(_16R),
    .in17(_17R), .in18(_18R), .in19(_19R), .in20(_20R), .in21(_21R), .in22(_22R), .in23(_23R), .in24(_24R),
    .in25(_25R), .in26(_26R), .in27(_27R), .in28(_28R), .in29(_29R), .in30(_30R), .in31(_31R), .out(RD1),
    .sel(RA));
  Multiplexer #(.select(5), .width(32), .enable("false")) multiplexer_2 (
    .in0(_0R), .in1(_1R), .in2(_2R), .in3(_3R), .in4(_4R), .in5(_5R), .in6(_6R), .in7(_7R), .in8(_8R),
    .in9(_9R), .in10(_10R), .in11(_11R), .in12(_12R), .in13(_13R), .in14(_14R), .in15(_15R), .in16(_16R),
    .in17(_17R), .in18(_18R), .in19(_19R), .in20(_20R), .in21(_21R), .in22(_22R), .in23(_23R), .in24(_24R),
    .in25(_25R), .in26(_26R), .in27(_27R), .in28(_28R), .in29(_29R), .in30(_30R), .in31(_31R), .out(RD2),
    .sel(RB));

  // Other names for the same wires on the sheet: EN = Write_Enable
endmodule

module jr (
  input  O5,
  input  O4,
  input  O3,
  input  O2,
  input  O1,
  input  O0,
  input  F5,
  input  F4,
  input  F3,
  input  F2,
  input  F1,
  input  F0,
  output jr
);

  wire not_1_out, not_2_out, not_3_out, not_4_out, not_5_out, not_6_out, not_7_out, not_8_out, not_9_out,
       not_10_out, not_11_out, not_12_out;

  not not_1 (not_1_out, O5);
  not not_2 (not_2_out, O4);
  not not_3 (not_3_out, O3);
  not not_4 (not_4_out, O2);
  not not_5 (not_5_out, O1);
  not not_6 (not_6_out, O1);
  not not_7 (not_7_out, F5);
  not not_8 (not_8_out, F4);
  not not_9 (not_9_out, F2);
  not not_10 (not_10_out, F1);
  not not_11 (not_11_out, F1);
  not not_12 (not_12_out, F0);
  and and_1 (jr, not_1_out, not_2_out, not_3_out, not_4_out, not_5_out, not_6_out, not_7_out, not_8_out, F3, not_9_out, not_10_out, not_11_out, not_12_out);
endmodule
